# Fritzing sketch circuito (saved by Fritzing 0.9.5d)
breadboards: 1

parts:
  Componente2 = InvenSense MPU6050
  WeMos_D1_Mini2 = WeMos D1 Mini
  M2 = MAX30102
  Water_Level_Sensor1 = Water Level Sensor
  DHT2 = DHT11 Humitidy and Temperature Sensor
  Mod2 = KY-026 Flame Sensor Module [package="Breakout board"]
  Sensor2 = Gas Sensor Breakout Board
  Mod3 = KY-012 Active Buzzer Module [package="Breakout board"]

nets:
  VCC: Componente2.VCC, WeMos_D1_Mini2.5V, M2.VIN, Water_Level_Sensor1.VCC, DHT2.VDD, Mod2.+, Sensor2.5V, Mod3.NC
  GND: Componente2.GND, WeMos_D1_Mini2.G, M2.SCL, M2.SDA, M2.IRQ, M2.RD, M2.GND, Water_Level_Sensor1.GND, DHT2.GND, Mod2.G, Sensor2.GND, Mod3.-
  N1: Componente2.SCL, Componente2.SDA, Componente2.XDA, Componente2.XCL, Componente2.AD0
  N2: WeMos_D1_Mini2.A0, Water_Level_Sensor1.SIG
  N3: WeMos_D1_Mini2.D0, Mod3.S
  N4: WeMos_D1_Mini2.D1, WeMos_D1_Mini2.D2
  N5: WeMos_D1_Mini2.D5, DHT2.DATA
  N6: WeMos_D1_Mini2.D6, Sensor2.DOUT
  N7: WeMos_D1_Mini2.D7, Mod2.D0

custom parts:
  MAX30102: Oximeter module using the MAX30102 chip. You may wish to read (and check your module) this post on power problems with these modules: https://reedpaper.wordpress.com/2018/08/22/pulse-oximeter-max30100-max30102-how-to-fix-wrong-board/ . As usual, if you want the mounting holes in pcb, you need to drag a hole over the pad in silkscreen to actually drill the hole (by default they are not drilled)
  Water Level Sensor: A water level sensor. This sensor operates at 3V to 5V. The Sig (signal) pin outputs an analogue signal that is in proportion to the amount of water in contact with the sensor.
  DHT11 Humitidy and Temperature Sensor: DHT11 Humidity and Temperature Sensor
  KY-026 Flame Sensor Module: KY-026 Flame Sensor Module reacts in the presence of fire.
  Gas Sensor Breakout Board: Gas sensor breakout board. Input voltage is 5V. Sensor output is available in analog and digital.
  KY-012 Active Buzzer Module: Active Piezoelectric Buzzer Module KY-012, it produces single-tone sound when signal is high. (Special thanks to vanepp for fixing the PCB holes and other errors)
